// Digital circuit addressDecoder.dig as structural Verilog
module addressDecoder (
  input  A15,
  input  A14,
  input  A13,
  input  A12,
  input  A11,
  input  A10,
  input  A9,
  input  GND,
  input  plus_5V,
  input  PHI2,
  input  R_W,
  output RAMCS,
  output ROMCS,
  output IOCS1,
  output IOCS2,
  output IOCS3,
  output IOCS4,
  output WE,
  output OE,
  output IOCS5,
  output IOCS6
);

  wire or_1_out;

  or or_1 (or_1_out, A14, A13, A12);
  nand nand_1 (OE, R_W, R_W);
  _74138 _74138_1 (
    .pin1(A9), .pin2(A10), .pin3(A11), .pin4(or_1_out), .pin5(GND), .pin6(A15), .pin8(GND), .pin10(IOCS6),
    .pin11(IOCS5), .pin12(IOCS4), .pin13(IOCS3), .pin14(IOCS2), .pin15(IOCS1), .pin16(plus_5V));  // open: pin7, pin9
  nand nand_2 (WE, OE, PHI2);
  nand nand_3 (ROMCS, A15, or_1_out);

  assign RAMCS = A15;

  // Notes on the sheet:
  //   plus_5V: default 1
endmodule
